# Fritzing sketch CoffeeThermometer (saved by Fritzing 0.9.0b)

parts:
  Part1 = LilyPad Temperature Sensor
  Part2 = LilyPad Tri-Color LED
  Part4 = Lilypad Arduino Board
  Part5 = LilyPad Coin Cell Battery Holder

nets:
  VCC: Part1.VCC, Part2.+, Part4.VCC, Part5.+
  GND: Part1.GND, Part4.GND, Part5.-
  N1: Part1.VO, Part4.A1
  N2: Part2.R, Part4.D10
  N3: Part2.B, Part4.D9
